# Fritzing sketch Humidity and temp on  20x4 LCD (saved by Fritzing 0.9.3b)
breadboards: 1

parts:
  Part1 = Arduino Uno (Rev3)
  LCD_20x4_I2C = Grove OLED 128x96
  RHT1 = Humidity and Temperature Sensor RHT03

nets:
  N1: Part1.A4/SDA, LCD_20x4_I2C.SDA
  N2: Part1.A5/SCL, LCD_20x4_I2C.SCL
  N3: Part1.D2, RHT1.Data-signal
  VCC: Part1.5V, LCD_20x4_I2C.VCC, RHT1.Vcc
  GND: Part1.GND, LCD_20x4_I2C.GND, RHT1.GND_2

// code stored in the sketch: LCDHumidity.ino
#include <Wire.h> 
#include <LiquidCrystal.h>
#include "LiquidCrystal_I2C.h"
#include"DHT.h"   //dht lib
#define DHTPIN 2   //data pin for humidity sensor
#define DHTTYPE DHT22 //setup dht22
DHT dht(DHTPIN,DHTTYPE);

// Set the LCD address to 0x27 for a 16 chars and 2 line display
LiquidCrystal_I2C lcd(0x27, 16, 2);

void setup()
{
	// initialize the LCD
	lcd.begin();

	// Turn on the blacklight and print a message.
	lcd.backlight();
	lcd.print("TEMP, HUMIDITY");
}

void loop()
{
	  // Wait a few seconds between measurements.
  delay(2000);

  // Reading temperature or humidity takes about 250 milliseconds!
  // Sensor readings may also be up to 2 seconds 'old' (its a very slow sensor)
  float h = dht.readHumidity();
  // Read temperature as Celsius (the default)
  float t = dht.readTemperature();
  // Read temperature as Fahrenheit (isFahrenheit = true)
  float f = dht.readTemperature(true);

  // Check if any reads failed and exit early (to try again).
  if (isnan(h) || isnan(t) || isnan(f)) {
        lcd.print("Failed to read from DHT sensor!");
    return;
  }

  // Compute heat index in Fahrenheit (the default)
  float hif = dht.computeHeatIndex(f, h);
  // Compute heat index in Celsius (isFahreheit = false)
  float hic = dht.computeHeatIndex(t, h, false);
  lcd.setCursor(0,0);
  lcd.print("Humidity:    ");
  lcd.print(h);
  lcd.setCursor(0,1);
  lcd.print("Temperature: ");
  lcd.print(t);
  lcd.print("C ");
  lcd.setCursor(13,2);
  lcd.print(f);
  lcd.print("F");
  
*/
}
