# Fritzing sketch Controle-de-Acesso-com-ESP32-RFID-RC222-RELE-LEDs-CARTAOMESTRE (saved by Fritzing 0.9.10b)
breadboards: 1

parts:
  LCD2004-I2C1 = LCD2004-I2C
  Componente2 = part.prefix101218 [part_number=101218]
  LED1 = smd LED [color="Red (633nm)" package="1206 [SMD]"]
  LED2 = smd LED [color="Blue (430nm)" package="1206 [SMD]"]
  LED3 = smd LED [color="Green (555nm)" package="1206 [SMD]"]
  Botão_WIPE_da_gravação_dos_cartões = Pushbutton [package="[THT]"]
  Sensor_da_porta_aberta = Pushbutton [package="[THT]"]
  R1 = Resistor [tolerance=±5% power=0.25 resistance=220 package=THT]
  R2 = Resistor [tolerance=±5% power=0.25 resistance=220 package=THT]
  R3 = Resistor [tolerance=±5% power=0.25 resistance=220 package=THT]
  Power_plug1 = Power plug
  MH-ET_LIVE_ESP32_DEVKIT1 = MH-ET LIVE ESP32 DEVKIT
  Botão_para_Abrir_a_Porta = Pushbutton [package="[THT]"]
  LED4 = smd LED [color="Red (633nm)" package="1206 [SMD]"]
  R4 = Resistor [tolerance=±5% power=0.25 resistance=220 package=THT]  # not connected
  R5 = Resistor [tolerance=±5% power=0.25 resistance=220 package=THT]  # not connected
  R6 = Resistor [tolerance=±5% power=0.25 resistance=220 package=THT]
  J1 = Piezo Speaker

nets:
  N1: LCD2004-I2C1.connector0, Botão_WIPE_da_gravação_dos_cartões.Pin_3, Botão_WIPE_da_gravação_dos_cartões.Pin_4, Sensor_da_porta_aberta.Pin_3, Sensor_da_porta_aberta.Pin_4, MH-ET_LIVE_ESP32_DEVKIT1.connector62, Botão_para_Abrir_a_Porta.Pin_3, Botão_para_Abrir_a_Porta.Pin_4, J1.pin1
  N2: LCD2004-I2C1.connector1, MH-ET_LIVE_ESP32_DEVKIT1.connector63
  N3: LCD2004-I2C1.connector2, MH-ET_LIVE_ESP32_DEVKIT1.connector69
  N4: LCD2004-I2C1.connector3, MH-ET_LIVE_ESP32_DEVKIT1.connector66
  N5: Componente2.connector8, MH-ET_LIVE_ESP32_DEVKIT1.connector73
  N6: Componente2.connector9, MH-ET_LIVE_ESP32_DEVKIT1.connector72
  N7: Componente2.connector10, MH-ET_LIVE_ESP32_DEVKIT1.connector65
  N8: Componente2.connector11, MH-ET_LIVE_ESP32_DEVKIT1.connector71
  N9: Componente2.connector13, LED1.cathode, LED2.cathode, LED3.cathode, Power_plug1.GND, MH-ET_LIVE_ESP32_DEVKIT1.connector64, LED4.cathode
  N10: Componente2.connector14, MH-ET_LIVE_ESP32_DEVKIT1.connector78
  N11: Componente2.connector15, MH-ET_LIVE_ESP32_DEVKIT1.connector45
  N12: LED1.anode, R1.Pin_1
  N13: LED2.anode, R3.Pin_1
  N14: LED3.anode, R2.Pin_1
  N15: Botão_WIPE_da_gravação_dos_cartões.Pin_1, Botão_WIPE_da_gravação_dos_cartões.Pin_2, MH-ET_LIVE_ESP32_DEVKIT1.connector52
  N16: Sensor_da_porta_aberta.Pin_1, Sensor_da_porta_aberta.Pin_2, MH-ET_LIVE_ESP32_DEVKIT1.connector76
  N17: R1.Pin_0, MH-ET_LIVE_ESP32_DEVKIT1.connector55
  N18: R2.Pin_0, MH-ET_LIVE_ESP32_DEVKIT1.connector54
  N19: R3.Pin_0, MH-ET_LIVE_ESP32_DEVKIT1.connector53
  N20: MH-ET_LIVE_ESP32_DEVKIT1.connector74, J1.pin2
  N21: MH-ET_LIVE_ESP32_DEVKIT1.connector75, R6.Pin_0
  N22: MH-ET_LIVE_ESP32_DEVKIT1.connector79, Botão_para_Abrir_a_Porta.Pin_1, Botão_para_Abrir_a_Porta.Pin_2
  N23: LED4.anode, R6.Pin_1
