# Fritzing sketch rfid-rc522 (saved by Fritzing 0.9.3b)
circuit board: 8.46667cm x 5.64444cm
breadboards: 1

parts:
  Componente1 = RFID-RC522-v2
  LCD1 = LCD screen
  Componente2 = Arduino Mega 2560 (Rev3)
  R1 = Rotary Potentiometer (Small) [maximum_resistance=100kΩ package=THT]
  LED1 = DUO LED RG [package="5 mm [THT]"]
  R2 = Resistor [tolerance=±5% resistance=220 package=THT]

nets:
  N1: Componente1.SDA, Componente2.D53
  N2: Componente1.SCK, Componente2.D52
  N3: Componente1.MOSI, Componente2.D51
  N4: Componente1.MISO, Componente2.D50
  GND: Componente1.GND, LCD1.VSS, LCD1.R/W, LCD1.LED-, Componente2.GND, R1.leg1, R2.Pin_0
  N5: Componente1.RST, Componente2.D6_PWM
  3.3V: Componente1.3.3V, Componente2.3V3
  VDD: LCD1.VDD, LCD1.LED+, Componente2.5V, R1.leg2
  N6: LCD1.V0, R1.wiper
  N7: LCD1.RS, Componente2.D12_PWM
  N8: LCD1.E, Componente2.D11_PWM
  N9: LCD1.DB4, Componente2.D5_PWM
  N10: LCD1.DB5, Componente2.D4_PWM
  N11: LCD1.DB6, Componente2.D3_PWM
  N12: LCD1.DB7, Componente2.D2_PWM
  N13: Componente2.D8_PWM, LED1.red_anode
  N14: Componente2.D7_PWM, LED1.green_anode
  N15: LED1.common_cathode, R2.Pin_1

custom parts:
  RFID-RC522-v2: A simple China made RFID-RC522 Reader; do check the pin labels, as this is a MFRC522 based clone.

// code stored in the sketch: Untitled2.ino
/*
 * 
 * All the resources for this project: http://randomnerdtutorials.com/
 * Modified by José Vicente
 * 
 * Created by Japtech
 * 
 */
 
#include <SPI.h>
#include <MFRC522.h>
#include <LiquidCrystal.h>
 
#define SS_PIN 53
#define RST_PIN 6
LiquidCrystal lcd(12, 11, 5, 4, 3, 2);

MFRC522 mfrc522(SS_PIN, RST_PIN);   // Create MFRC522 instance.

void setup() 
{
  lcd.begin(16, 2);
  pinMode(7, OUTPUT);
  pinMode(8, OUTPUT);
  Serial.begin(9600);   // Initiate a serial communication
  SPI.begin();      // Initiate  SPI bus
  mfrc522.PCD_Init();   // Initiate MFRC522
  Serial.println("Approximate your card to the reader...");
  Serial.println();
  lcd.print("waiting for card");
}
void loop() 
{
  // Look for new cards
  
  if ( ! mfrc522.PICC_IsNewCardPresent()) 
  {
    return;
  }
  // Select one of the cards
  if ( ! mfrc522.PICC_ReadCardSerial()) 
  {
    return;
  }
  //Show UID on serial monitor
  Serial.print("UID tag :");
  String content= "";
  byte letter;
  for (byte i = 0; i < mfrc522.uid.size; i++) 
  {
     Serial.print(mfrc522.uid.uidByte[i] < 0x10 ? " 0" : " ");
     Serial.print(mfrc522.uid.uidByte[i], HEX);
         
     content.concat(String(mfrc522.uid.uidByte[i] < 0x10 ? " 0" : " "));
     content.concat(String(mfrc522.uid.uidByte[i], HEX));
  }
  Serial.println();
  Serial.print("Message : ");
  content.toUpperCase();
  if (content.substring(1) == "63 8C E5 C7") //change here the UID of the card/cards that you want to give access
  {
    Serial.println("Authorized access");
    lcd.clear();
    lcd.print("Authorized access");
    digitalWrite(7, HIGH);
    delay(3000);
    digitalWrite(7, LOW);
    lcd.clear();
    lcd.print("waiting for card");
    Serial.println();
  }
 
 else   {
    Serial.println(" Access denied");
    lcd.clear();
    lcd.print(" Access denied");
    digitalWrite(8, HIGH);
    delay(3000);
    digitalWrite(8, LOW);
    lcd.clear();
    lcd.print("waiting for card");
  }
}
